# Fritzing sketch modbus2 (saved by Fritzing 0.9.5d)
circuit board: 8.46667cm x 5.64444cm
perfboards: 1

parts:
  パーツ2 = Arduino Pro Mini v13
  J16 = screw terminal, 4 pins
  U6 = 74HC165 [part_number=SN74LS165 package="DIP16 [THT]"]
  U7 = 74HC165 [part_number=SN74LS165 package="DIP16 [THT]"]
  RE6 = Hexadecimal Rotary Encoder [part_number=APEM-PT65-303 package=THT]
  RE7 = Hexadecimal Rotary Encoder [part_number=APEM-PT65-303 package=THT]
  R33 = Resistor [tolerance=±5% resistance=2000 package=THT]
  R34 = Resistor [tolerance=±5% resistance=2000 package=THT]
  R35 = Resistor [tolerance=±5% resistance=2000 package=THT]
  R36 = Resistor [tolerance=±5% resistance=2000 package=THT]
  R37 = Resistor [tolerance=±5% resistance=2000 package=THT]
  R38 = Resistor [tolerance=±5% resistance=2000 package=THT]
  R39 = Resistor [tolerance=±5% resistance=2000 package=THT]
  R40 = Resistor [tolerance=±5% resistance=2000 package=THT]  # not connected
  RE8 = Hexadecimal Rotary Encoder [part_number=APEM-PT65-303 package=THT]
  R41 = Resistor [tolerance=±5% resistance=100 package=THT]
  R42 = Resistor [tolerance=±5% resistance=０ package=THT]
  R43 = Resistor [tolerance=±5% resistance=０ package=THT]
  R44 = Resistor [tolerance=±5% resistance=０ package=THT]
  R45 = Resistor [tolerance=±5% resistance=０ package=THT]
  R46 = Resistor [tolerance=±5% resistance=2000 package=THT]
  R47 = Resistor [tolerance=±5% resistance=2000 package=THT]
  R48 = Resistor [tolerance=±5% resistance=2000 package=THT]
  R49 = Resistor [tolerance=±5% resistance=2000 package=THT]
  J17 = female pin header, 3 pins [form="♀ (female)"]
  J18 = female pin header, 6 pins [form="♀ (female)"]
  J19 = female pin header, 1 pin [form="♀ (female)"]
  J20 = female pin header, 1 pin [form="♀ (female)"]
  J21 = female pin header, 4 pins [form="♀ (female)"]
  J22 = female pin header, 4 pins [form="♀ (female)"]
  J23 = Screw terminal - 2 pins [package=THT]  # not connected
  J24 = female pin header, 3 pins [form="♀ (female)"]
  R50 = Resistor [tolerance=±5% resistance=０ package=THT]
  R51 = Resistor [tolerance=±5% resistance=０ package=THT]
  J25 = female pin header, 6 pins [form="♀ (female)"]
  U8 = SWITCH_SPDT [package=kps-1290]
  R52 = Resistor [tolerance=±5% resistance=100 package=THT]
  C3 = Capacitor [package=cap-pth-5mm]  # not connected
  C4 = Ceramic Capacitor [capacitance=100nF package="200 mil [THT, multilayer]"]
  J26 = female pin header, 9 pins [form="♀ (female)"]
  R56 = Resistor [tolerance=±5% resistance=０ package=THT]
  R57 = Resistor [tolerance=±5% resistance=０ package=THT]
  R58 = Resistor [tolerance=±5% resistance=０ package=THT]
  R59 = Resistor [tolerance=±5% resistance=０ package=THT]

nets:
  N1: パーツ2.GND, J17.pin3, J26.pin9
  N2: パーツ2.RESET, J17.pin2
  N3: パーツ2.VCC, J16.pin1, J16.pin2, R37.Pin_1, R39.Pin_1, J17.pin1, J18.pin1, J21.pin1
  N4: パーツ2.A1, R50.Pin_1, J25.pin6
  N5: パーツ2.A0, R51.Pin_1, J25.pin5
  N6: パーツ2.D13/SCK, J16.pin4, J25.pin4
  N7: パーツ2.D12/MISO, J16.pin3, J25.pin3
  N8: パーツ2.D11_PWM/MOSI, J25.pin2, R58.Pin_0
  N9: パーツ2.D10_PWM/SS, J25.pin1, R57.Pin_1
  N10: パーツ2.D9_PWM, J18.pin4, J26.pin1
  N11: パーツ2.D8, J18.pin3, J26.pin2
  N12: パーツ2.D7, U7.Q1, J26.pin3
  N13: パーツ2.D6_PWM, R43.Pin_1, J26.pin4
  N14: パーツ2.D5_PWM, U7.Q7', R45.Pin_1, J26.pin5
  N15: パーツ2.D4, J22.pin1, J26.pin6
  N16: パーツ2.D3_PWM, J22.pin2, J22.pin3, J26.pin7
  N17: パーツ2.D2, J22.pin4, J26.pin8
  N18: U6.Q1, U7.Q2
  N19: U6.Q3, RE7.Output1Pin, R34.Pin_0
  N20: U6.Q4, RE7.Output4Pin, R36.Pin_0
  N21: U6.Q5, RE7.Output8pin, R35.Pin_0
  N22: U6.Q6, RE7.Output2Pin, R33.Pin_1
  N23: U6.Q7', R45.Pin_0
  N24: U6.MR, U7.MR, R43.Pin_0
  N25: U6.ST_CP, R44.Pin_0
  N26: U6.OE, RE6.Output8pin, R38.Pin_0
  N27: U6.DS, RE6.Output2Pin, R37.Pin_0
  N28: U7.Q3, RE8.Output1Pin, R48.Pin_0
  N29: U7.Q4, RE8.Output4Pin, R49.Pin_0
  N30: U7.Q5, RE8.Output8pin, R47.Pin_0
  N31: U7.Q6, RE8.Output2Pin, R46.Pin_0
  N32: U7.Q7, R34.Pin_1, R35.Pin_1, R36.Pin_1, R46.Pin_1, R47.Pin_1, R48.Pin_1
  N33: U7.GND, U8.O, R56.Pin_1
  N34: U7.SH_CP, U8.P
  N35: RE6.Output1Pin, R39.Pin_0
  N36: RE6.Output4Pin, R44.Pin_1
  N37: RE6.InputCommon, RE6.InputCommon2, RE7.InputCommon, RE7.InputCommon2, R42.Pin_1, J21.pin4, J24.pin3
  N38: RE8.InputCommon, RE8.InputCommon2, R42.Pin_0, R56.Pin_0
  N39: R41.Pin_1, J19.pin1
  N40: J18.pin2, R59.Pin_1
  N41: J18.pin5, R57.Pin_0
  N42: J18.pin6, R58.Pin_1
  N43: J20.pin1, R50.Pin_0
  N44: J24.pin2, R51.Pin_0
  N45: U8.S, R52.Pin_1, C4.1
  N46: R52.Pin_0, C4.0

custom parts:
  74HC165: 8-bit parallel-load shift registers
